# Fritzing sketch ringer2 (saved by Fritzing 0.9.3b)
circuit board: 8.53488cm x 5.63626cm
breadboards: 1

parts:
  Q1 = Basic FET P-Channel [package="TO220 [THT]"]
  J1 = Screw terminal - 2 pins [package=THT]  # not connected
  J2 = Screw terminal - 2 pins [package=THT]  # not connected
  J3 = Screw terminal - 2 pins [package=THT]  # not connected
  J4 = Screw terminal - 2 pins [package=THT]  # not connected
  Raspberry_Pi_1 = Raspberry Pi 3 [part_number=RPI-3-V1.2]
  L1 = RCP1317 [package="13 cm [THT]"]
  R2 = Resistor [tolerance=±5% resistance=180 package=THT]
  IC1 = MC34063AP [chip_label=IC package="DIP (Dual Inline) [THT]"]
  D1 = Schottky Diode [part_number=1N5817 package="300 mil [THT]"]
  R4 = Resistor [tolerance=±5% resistance=47k package=THT]
  R3 = Resistor [tolerance=±5% resistance=1k package=THT]
  R1 = 0.22 Ω Resistor [package=THT]
  C1 = Ceramic Capacitor [capacitance=1nF package="100 mil [THT, multilayer]"]
  C2 = Electrolytic Capacitor [capacitance=100µF voltage=50V package="200 mil [THT, electrolytic]"]
  LED1 = LED - 3mm [color="Red (633nm)" package="3 mm [THT]"]
  IC2 = NJM2670 [package="NJM2670D2 (DIP22)"]
  R5 = Resistor [tolerance=±5% resistance=1k package=THT]
  U1 = RELAY [package=OJ]  # not connected

nets:
  N1: Q1.gate, Raspberry_Pi_1.GPIO4
  VCC: Q1.drain, IC1.VCC, R1.Pin_1, IC2.ENABLE_A, IC2.VCC, R5.Pin_0
  N2: Q1.source, Raspberry_Pi_1.5V
  GND: Raspberry_Pi_1.GND, IC1.Switch_Emitter, IC1.GND, R3.Pin_1, C1.0, C2.+, LED1.anode, IC2.SENSE_A, IC2.GND, IC2.ENABLE_B
  N3: Raspberry_Pi_1.GPIO5, IC2.IN_A
  N4: Raspberry_Pi_1.GPIO6, IC2.IN_A2
  N5: L1.pin_0, IC1.Switch_Collector, D1.cathode
  N6: L1.pin_1, R2.Pin_1, IC1.Ipk, R1.Pin_0
  N7: R2.Pin_0, IC1.Drive_Collector
  N8: IC1.Timing_Capacitor, C1.1
  N9: IC1.Comparator_Inverting_Input, R4.Pin_0, R3.Pin_0
  N10: D1.anode, R4.Pin_1, C2.-, IC2.VS_A
  N11: LED1.cathode, R5.Pin_1

notes:
  * Adjust boost/buck resistors to dial in ~30v
  * Ensure diode, cap polarity is correct
  * Add decoupling

custom parts:
  RCP1317: Inductor
  0.22 Ω Resistor: BPR58 0.22 Ω 5W Resistor
