# Fritzing sketch ringer3 (saved by Fritzing 0.9.3b)
circuit board: 8.53488cm x 5.63626cm
breadboards: 1

parts:
  Q1 = Basic FET P-Channel [package="TO220 [THT]"]
  Bell_Out = Screw terminal - 2 pins [package=THT]
  Bell_In = Screw terminal - 2 pins [package=THT]
  Magneto = Screw terminal - 2 pins [package=THT]
  Hook = Screw terminal - 2 pins [package=THT]
  Raspberry_Pi_1 = Raspberry Pi 3 [part_number=RPI-3-V1.2]
  ACT = LED - 3mm [color="Red (633nm)" package="3 mm [THT]"]
  IC2 = NJM2670 [package="NJM2670D2 (DIP22)"]
  R2 = Resistor [tolerance=±5% resistance=180 package=THT]
  D1 = Schottky Diode [part_number=1N5817 package="300 mil [THT]"]
  R1 = Resistor [tolerance=±5% resistance=1k package=THT]
  C1 = Ceramic Capacitor [capacitance=1nF package="100 mil [THT, multilayer]"]
  C4 = Electrolytic Capacitor [capacitance=100µF voltage=50V package="200 mil [THT, electrolytic]"]
  R4 = Resistor [tolerance=±5% resistance=47k package=THT]
  R5 = Resistor [tolerance=±5% resistance=1k package=THT]
  IC1 = MC34063AP [chip_label=IC package="DIP (Dual Inline) [THT]"]
  C2 = Electrolytic Capacitor [capacitance=100µF package="100 mil [THT, electrolytic]"]
  C3 = Ceramic Capacitor [capacitance=100nF package="100 mil [THT, multilayer]"]
  C5 = Electrolytic Capacitor [capacitance=3.3µF voltage=50V package="100 mil [THT, electrolytic]"]
  D2 = Rectifier Diode [part_number=1N4001 package="300 mil [THT]"]
  D3 = Rectifier Diode [part_number=1N4001 package="300 mil [THT]"]
  L1 = RCP1317 [package="13 cm [THT]"]
  R3 = 0.22 Ω Resistor [package=THT]
  U1 = RT314F03 [part_number=RT314F03 package=OJ]

nets:
  N1: Q1.gate, Raspberry_Pi_1.GPIO4
  VCC: Q1.drain, IC2.ENABLE_A, IC2.VCC, R5.Pin_0, IC1.VCC, C2.+, C3.0, R3.Pin_0
  N2: Q1.source, Raspberry_Pi_1.5V
  N3: Bell_Out.pin1, Bell_In.pin1, IC2.OUT_A1
  N4: Bell_Out.pin2, C5.-, U1.12#5, U1.11, U1.14
  N5: Bell_In.pin2, U1.12#4
  GND: Magneto.pin1, Hook.pin1, Raspberry_Pi_1.GND, ACT.cathode, IC2.SENSE_A, IC2.GND, IC2.ENABLE_B, R1.Pin_1, C1.0, C4.-, IC1.Switch_Emitter, IC1.GND, C2.-, C3.1, D2.cathode, D3.cathode
  N6: Magneto.pin2, Raspberry_Pi_1.GPIO19
  N7: Hook.pin2, Raspberry_Pi_1.GPIO26
  3V3: Raspberry_Pi_1.3v3, Raspberry_Pi_1.3V3, U1.A3
  N8: Raspberry_Pi_1.GPIO27, IC2.IN_A
  N9: Raspberry_Pi_1.GPIO22, IC2.IN_A2
  N10: Raspberry_Pi_1.GPIO6, D2.anode, U1.A2
  N11: Raspberry_Pi_1.GPIO13, D3.anode, U1.A1
  N12: ACT.anode, R5.Pin_1
  N13: IC2.OUT_A2, C5.+
  N14: IC2.VS_A, D1.anode, C4.+, R4.Pin_1
  N15: R2.Pin_0, IC1.Drive_Collector
  N16: R2.Pin_1, IC1.Ipk, L1.pin_0, R3.Pin_1
  N17: D1.cathode, IC1.Switch_Collector, L1.pin_1
  N18: R1.Pin_0, R4.Pin_0, IC1.Comparator_Inverting_Input
  N19: C1.1, IC1.Timing_Capacitor

notes:
  * Adjust boost/buck resistors to dial in ~30v
  cranky rev. A
  Magneto
  Driver
  +3.3v

custom parts:
  RCP1317: Inductor
  0.22 Ω Resistor: BPR58 0.22 Ω 5W Resistor
  RT314F03: Two-coil bistable SPDT Relay
